# Fritzing sketch Untitled Sketch 3 (saved by Fritzing 1.0.7)

parts:
  M1 = NRF24L01-BO [package=THT]
  OLED2 = OLED 128x64 I2C Monochrome Display GND-VDD
  Mod1 = Raspberry Pi Pico

nets:
  N1: M1.IRQ, Mod1.pin_17
  N2: M1.M1, Mod1.pin_21
  N3: M1.M0, Mod1.pin_25
  N4: M1.SCK, Mod1.pin_24
  N5: M1.CSN, Mod1.pin_20
  N6: M1.CE, Mod1.pin_19
  GND: M1.GND, OLED2.GND, Mod1.pin_18, Mod1.pin_33, Mod1.pin_38, Mod1.pin_42
  VCC: M1.VCC, OLED2.VDD, Mod1.pin_40
  N7: OLED2.SCK, Mod1.pin_7
  N8: OLED2.SDA, Mod1.pin_6

custom parts:
  NRF24L01-BO: NRF24L01-BO breakout board for the NRF24L01. Pcb view suppressed as unneeded.
  OLED 128x64 I2C Monochrome Display GND-VDD: OLED 128x64 I2C Monochrome Display. Note: there are two variants of this part, this one is the GND VDD SCK SDA variant. The other is VDD GND SCK SDA. Make sure you select the part that matches your module as using the incorrect part will probably destroy your module! In addition the mounting holes are marked on silkscreen but not by default drilled. If you want drilled mounting holes, copy a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
  Raspberry Pi Pico: Raspberry Pi Pico. Based around the RP2040 microcontroller the Pico is a low cost microcontroller device bringing Raspberry Pi quality, cost, and easy of use to the microcontroller space. Jan 2021, Split part in to two versions: SMD (this one) and tht. This one is single sided and uses the castellation pads to solder the module to the board (no holes, other than for the USB connector!). The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
