# Fritzing sketch lights (saved by Fritzing 1.0.7)

parts:
  M1 = NRF24L01-BO [package=THT]
  Mod1 = Raspberry Pi Pico
  Sensor1 = TTP223B Capacitive Touch Sensor Module
  U1 = 4-Channel 5v Relay Shield [package=relay-4ch5v10a]

nets:
  N1: M1.IRQ, Mod1.pin_17
  N2: M1.M1, Mod1.pin_21
  N3: M1.M0, Mod1.pin_25
  N4: M1.SCK, Mod1.pin_24
  N5: M1.CSN, Mod1.pin_20
  N6: M1.CE, Mod1.pin_19
  GND: M1.GND, Mod1.pin_3, Mod1.pin_18, Mod1.pin_33, Mod1.pin_38, Mod1.pin_42, Sensor1.GND, U1.GND
  VCC: M1.VCC, Mod1.pin_40, Sensor1.VCC, U1.VCC
  N7: Mod1.pin_5, Sensor1.SIG
  N8: Mod1.pin_7, U1.IN1
  N9: Mod1.pin_9, U1.IN2
  N10: Mod1.pin_10, U1.IN3
  N11: Mod1.pin_11, U1.IN4

custom parts:
  NRF24L01-BO: NRF24L01-BO breakout board for the NRF24L01. Pcb view suppressed as unneeded.
  Raspberry Pi Pico: Raspberry Pi Pico. Based around the RP2040 microcontroller the Pico is a low cost microcontroller device bringing Raspberry Pi quality, cost, and easy of use to the microcontroller space. Jan 2021, Split part in to two versions: SMD (this one) and tht. This one is single sided and uses the castellation pads to solder the module to the board (no holes, other than for the USB connector!). The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
  TTP223B Capacitive Touch Sensor Module: The TTP223B capacitive touch sensor module uses the TTP223B IC. The appropriate voltage is approximately 2 to 5.5 volts.
  4-Channel 5v Relay Shield: 4 Channel 5v Relay Shield w. 2x SPD-06VDC-SD-C
